# Fritzing sketch ArduinoTwitter (saved by Fritzing 0.9.2b)
breadboards: 1

parts:
  Eleman1 = Arduino Uno (Rev3)
  J1 = Basic Servo
  Q1 = TRANSISTOR_NPN [package=to-92-ammo]
  R1 = Trimmer Potentiometer [maximum_resistance=10kΩ package=THT]
  R2 = Trimmer Potentiometer [maximum_resistance=10kΩ package=THT]
  U1 = LCD-16X2 [package=lcd-16x2_noholes]

nets:
  N1: Eleman1.A0, R1.wiper
  N2: Eleman1.D9_PWM, J1.pulse
  N3: Eleman1.D11_PWM/MOSI, U1.E
  N4: Eleman1.D12/MISO, U1.RS
  N5: Eleman1.D2, U1.DB7
  N6: Eleman1.D3_PWM, U1.DB6
  N7: Eleman1.D4, U1.DB5
  N8: Eleman1.D5_PWM, U1.DB4
  N9: Eleman1.D7, Q1.B
  N10: J1.gnd, Q1.C
  VCC: J1.vcc, U1.VDD, U1.A
  N11: Q1.E, R1.leg1, R2.leg1
  N12: R1.leg2, R2.leg2
  N13: R2.wiper, U1.VO
  N14: U1.VSS, U1.R_W, U1.K
