# Fritzing sketch ArduinoÇakar (saved by Fritzing 0.9.2b)
breadboards: 1

parts:
  U1 = POT [package=pot_mammoth]
  LED1 = smd LED [color="Red (633nm)" package="0603 [SMD]"]
  LED2 = smd LED [color="Red (633nm)" package="0603 [SMD]"]
  LED3 = smd LED [color="Blue (470nm)" package="0603 [SMD]"]
  LED4 = smd LED [color="Blue (470nm)" package="0603 [SMD]"]
  R1 = Resistor [tolerance=±5% resistance=220 package="1206 [SMD]"]
  R2 = Resistor [tolerance=±5% resistance=220 package="1206 [SMD]"]
  R3 = Resistor [tolerance=±5% resistance=220 package="1206 [SMD]"]
  R4 = Resistor [tolerance=±5% resistance=220 package="1206 [SMD]"]
  Eleman1 = Arduino Uno (Rev3)

nets:
  N1: U1.S, Eleman1.5V
  N2: U1.A, Eleman1.A0
  N3: U1.E, LED1.cathode, LED2.cathode, LED3.cathode, LED4.cathode, Eleman1.GND
  N4: LED1.anode, R1.Pin_0
  N5: LED2.anode, R2.Pin_0
  N6: LED3.anode, R3.Pin_0
  N7: LED4.anode, R4.Pin_0
  N8: R1.Pin_1, R2.Pin_1, Eleman1.D12/MISO
  N9: R3.Pin_1, R4.Pin_1, Eleman1.D11_PWM/MOSI
