# Fritzing sketch KarakterLCDOYUN (saved by Fritzing 0.9.2b)
breadboards: 1

parts:
  Eleman1 = Arduino Uno (Rev3)
  LCD1 = LCD screen  # not connected
  R1 = Trimmer Potentiometer [maximum_resistance=10kΩ package=THT]
  S1 = Pushbutton [package="[THT]"]
  R2 = Resistor [tolerance=±5% resistance=4.7k package=THT]

nets:
  N1: Eleman1.D7, S1.Pin_3, S1.Pin_4
  N2: Eleman1.5V, R1.leg2
  N3: Eleman1.GND, R1.leg1, R2.Pin_0
  N4: S1.Pin_1, S1.Pin_2, R2.Pin_1
