# Fritzing sketch RGBoyunu (saved by Fritzing 0.9.2b)
breadboards: 1

parts:
  S1 = Pushbutton [package="[THT]"]
  S2 = Pushbutton [package="[THT]"]
  R1 = Resistor [tolerance=±5% resistance=220 package=THT]
  R2 = Resistor [tolerance=±5% resistance=220 package=THT]
  R3 = Resistor [tolerance=±5% resistance=220 package=THT]
  R4 = Resistor [tolerance=±5% resistance=220 package=THT]
  R5 = Resistor [tolerance=±5% resistance=220 package=THT]
  Eleman1 = Arduino Uno (Rev3)
  LED1 = RGB LED (com. cathode, rbg) [package="5 mm [THT]"]  # not connected

nets:
  N1: S1.Pin_1, S1.Pin_2, Eleman1.RESET
  N2: S1.Pin_3, S1.Pin_4, R2.Pin_1
  N3: S2.Pin_1, S2.Pin_2, R1.Pin_1
  N4: S2.Pin_3, S2.Pin_4, Eleman1.D12/MISO
  N5: R1.Pin_0, Eleman1.GND
  N6: R2.Pin_0, Eleman1.5V
  N7: R3.Pin_0, Eleman1.D3_PWM
  N8: R4.Pin_0, Eleman1.D6_PWM
  N9: R5.Pin_0, Eleman1.D5_PWM

notes:
  1. Düğme Reset
  2. Düğme Kontrol
